# Fritzing sketch BTLED (saved by Fritzing 0.8.3b)
breadboards: 1

parts:
  元件6 = Bluetooth Mate Silver
  元件2 = Arduino Uno (Rev3)
  LED1 = LED - 5mm [color="Red (633nm)" package="5 mm [THT]"]

nets:
  N1: 元件6.TX_5V, 元件2.ICSP_MOSI, 元件2.D11_PWM/MOSI
  VCC: 元件6.VCC, 元件6.CTS_5V, 元件2.5V
  N2: 元件2.ICSP_SCK, 元件2.D13/SCK, LED1.anode
  N3: 元件2.GND, LED1.cathode

notes:
  STATE
  RXD
  TXD
  GND
  VCC
  EN
