# Fritzing sketch BTVR (saved by Fritzing 0.8.3b)
breadboards: 1

parts:
  元件6 = Bluetooth Mate Silver
  元件2 = Arduino Uno (Rev3)
  R1 = Rotary Potentiometer (Small)

nets:
  N1: 元件6.TX_5V, 元件2.ICSP_MOSI, 元件2.D11_PWM/MOSI
  VCC: 元件6.VCC, 元件6.CTS_5V, 元件2.5V, R1.leg1
  N2: 元件2.A0, R1.wiper
  N3: 元件2.GND, R1.leg2

notes:
  STATE
  RXD
  TXD
  GND
  VCC
  EN
